# Fritzing sketch Programming Board (saved by Fritzing 0.9.1b)
breadboards: 1

parts:
  J1 = AVR ISP 6 Pin [package=2x3_lock]
  U2 = atmega328 [package=dip]
  XTAL2 = Crystal [frequency="16 Mhz" package=THT]
  C1 = Ceramic Capacitor [capacitance="100 nF" package="1206 [SMD, multilayer]"]
  C3 = Capacitor [package=cap-pth-small2]
  C4 = Ceramic Capacitor [capacitance="100 nF" package="1206 [SMD, multilayer]"]
  C5 = Capacitor [package=cap-pth-small2]
  R1 = Resistor [tolerance=±20% resistance=10k package=THT]
  CONN2 = USB connector [package=THT]  # not connected
  J2 = AVR ISP 6 Pin [package=2x3_lock]

nets:
  N1: J1.1, J1.2, J2.1, J2.2
  N2: J1.3, J1.4, J2.3, J2.4
  N3: J1.5, J1.6, J2.5, J2.6
  N4: U2.RESET, R1.Pin_1
  N5: U2.VCC, U2.AVCC, XTAL2.pin_1, C1.1, C4.1, R1.Pin_0
  N6: U2.GND, XTAL2.pin_0, C1.0, C3.2, C4.0, C5.2
  N7: U2.XLAT1, C5.1
  N8: U2.XLAT2, C3.1

notes:
  USBtinyISP AVR Programmer
  -Allows manual uploading to the ATmega328P
  Adafruit AVR 6-pin ISP Breadboard adapter
